// Logisim project main.circ as structural Verilog: 1 circuit, main circuit main
module main (
);

  wire cdm_16_1_p3, cdm_16_1_p5, cdm_16_1_p6, cdm_16_1_p7, cdm_16_1_p8, dotmatrix_1_p4, dotmatrix_1_p5,
       not_1_out, ram_1_p4;
  wire [3:0] bit_extender_1_out, bit_extender_2_out;
  wire [15:0] cdm_16_1_p1, cdm_16_1_p2, cdm_16_1_p4, cdm_16_1_p9, cdm_16_1_p10, controlled_buffer_2_out;

  // CdM_16 cdm_16_1: pin names not known; wires that end beside it: cdm_16_1_p1, cdm_16_1_p2, cdm_16_1_p3, cdm_16_1_p4, cdm_16_1_p5, cdm_16_1_p6, cdm_16_1_p7, cdm_16_1_p8, cdm_16_1_p9, cdm_16_1_p10
  Bit_Extender #(.in_width(16), .out_width(4)) bit_extender_1 (.in(cdm_16_1_p1), .out(bit_extender_1_out));
  Bit_Extender #(.in_width(16), .out_width(4)) bit_extender_2 (.in(cdm_16_1_p2), .out(bit_extender_2_out));
  Clock clock_1 (.out(cdm_16_1_p3));
  // DotMatrix #(.matrixcols(16), .matrixrows(16)) dotmatrix_1: pin names not known; wires that end beside it: bit_extender_1_out, bit_extender_2_out, cdm_16_1_p4[1], dotmatrix_1_p4, dotmatrix_1_p5
  // display_controller display_controller_1: pin names not known; wires that end beside it: bit_extender_1_out, bit_extender_2_out, cdm_16_1_p4[1], dotmatrix_1_p4, dotmatrix_1_p5
  assign cdm_16_1_p10 = cdm_16_1_p6 ? controlled_buffer_2_out : 16'bz;  // Controlled_Buffer controlled_buffer_1
  assign controlled_buffer_2_out = not_1_out ? cdm_16_1_p9 : 16'bz;  // Controlled_Buffer controlled_buffer_2
  not not_1 (not_1_out, cdm_16_1_p6);
  // RAM ram_1: pin names not known; wires that end beside it: cdm_16_1_p8, cdm_16_1_p7, cdm_16_1_p5, ram_1_p4, cdm_16_1_p6, controlled_buffer_2_out
  Clock clock_2 (.out(ram_1_p4));

  // Notes on the sheet:
  //   Тут мы ставим кнопки для управления змеёй
  //   Тут мы ставим счётчик
endmodule
